// Logisim project Minmax4_CPU8.circ as structural Verilog: 1 circuit, main circuit main
module main (
  input  [7:0] in_1,
  input  [7:0] in_2,
  input  [7:0] in_3,
  input  [7:0] in_4
);

  wire ADD_EN, and_1_out, AND_EN, decoder_1_out0, decoder_1_out1, decoder_1_out2, decoder_1_out3, INV_EN,
       nor_1_out, not_1_out, or_1_out, OR_EN, ROT_EN, SUB_EN, undriven, XOR_EN;
  wire [1:0] ARG1, ARG2;
  wire [2:0] adder_1_out;
  wire [3:0] OPCODE;
  wire [7:0] adder_2_out, adder_3_out, and_2_out, multiplexer_2_out, not_2_out, or_2_out, PC_q, PM_dout,
       R0_q, R1_q, R2_q, SC_q, shifter_1_out, subtractor_1_out, xor_1_out;
  wire [7:3] adder_1_out_2;

  Adder adder_1 (.b(8'h1), .out({adder_1_out_2, adder_1_out}));  // open: a, cin, cout
  Decoder #(.enable("false"), .select(2)) decoder_1 (
    .out0(decoder_1_out0), .out1(decoder_1_out1), .out2(decoder_1_out2), .out3(decoder_1_out3), .sel(ARG1));
  Register PC (.D({adder_1_out_2, adder_1_out}), .en(undriven), .Q(PC_q));  // open: clk, clr
  Register R0 (.D({adder_1_out_2, adder_1_out}), .en(decoder_1_out1), .Q(R0_q));  // open: clk, clr
  Register R1 (.D({adder_1_out_2, adder_1_out}), .en(decoder_1_out2), .Q(R1_q));  // open: clk, clr
  Register R2 (.D({adder_1_out_2, adder_1_out}), .en(decoder_1_out3), .Q(R2_q));  // open: clk, clr
  Multiplexer #(.enable("true"), .select(2), .width(8)) multiplexer_1 (
    .in0(in_1), .in1(in_2), .in2(in_3), .in3(in_4), .out({adder_1_out_2, adder_1_out}), .sel(ARG2), .en(1'b0));
  and and_1 (and_1_out, 1'b0, nor_1_out);
  nor nor_1 (nor_1_out, ARG2[0], ARG2[1]);
  or or_1 (or_1_out, and_1_out, 1'b0);
  Adder adder_2 (.a(PC_q), .out(adder_2_out), .cin(or_1_out));  // open: b, cout
  Multiplexer #(.select(2), .width(8)) multiplexer_2 (
    .in0(PC_q), .in1(R0_q), .in2(R1_q), .in3(R2_q), .out(multiplexer_2_out), .sel(ARG1));
  Multiplexer #(.enable("true"), .select(2), .width(8)) multiplexer_3 (
    .in0(PM_dout), .in1(R0_q), .in2(R1_q), .in3(R2_q), .out({adder_1_out_2, adder_1_out}), .sel(ARG2),
    .en(not_1_out));
  not not_1 (not_1_out, 1'b0);
  RAM PM (.addr(adder_2_out), .dout(PM_dout));  // open: we, oe, clk, din
  assign {adder_1_out_2, adder_1_out} = ADD_EN ? adder_3_out : 8'bz;  // Controlled_Buffer controlled_buffer_1
  Adder adder_3 (.a(multiplexer_2_out), .b({adder_1_out_2, adder_1_out}), .out(adder_3_out));  // open: cin, cout
  assign {adder_1_out_2, adder_1_out} = SUB_EN ? subtractor_1_out : 8'bz;  // Controlled_Buffer controlled_buffer_2
  Subtractor subtractor_1 (
    .a(multiplexer_2_out), .b({adder_1_out_2, adder_1_out}), .out(subtractor_1_out));  // open: bin, bout
  assign and_2_out = multiplexer_2_out & {adder_1_out_2, adder_1_out};  // AND_Gate and_2, 8 bits wide
  assign {adder_1_out_2, adder_1_out} = AND_EN ? and_2_out : 8'bz;  // Controlled_Buffer controlled_buffer_3
  assign or_2_out = multiplexer_2_out | {adder_1_out_2, adder_1_out};  // OR_Gate or_2, 8 bits wide
  assign {adder_1_out_2, adder_1_out} = OR_EN ? or_2_out : 8'bz;  // Controlled_Buffer controlled_buffer_4
  assign xor_1_out = multiplexer_2_out ^ {adder_1_out_2, adder_1_out};  // XOR_Gate xor_1, 8 bits wide
  assign {adder_1_out_2, adder_1_out} = XOR_EN ? xor_1_out : 8'bz;  // Controlled_Buffer controlled_buffer_5
  assign not_2_out = ~multiplexer_2_out;  // NOT_Gate not_2, 8 bits wide
  assign {adder_1_out_2, adder_1_out} = INV_EN ? not_2_out : 8'bz;  // Controlled_Buffer controlled_buffer_6
  assign {adder_1_out_2, adder_1_out} = ROT_EN ? shifter_1_out : 8'bz;  // Controlled_Buffer controlled_buffer_7
  Shifter #(.shift("rl")) shifter_1 (.in(multiplexer_2_out), .\dist (adder_1_out), .out(shifter_1_out));
  Register INSTRUCTION (.D(PM_dout), .Q({ARG2, ARG1, OPCODE}));  // open: en, clk, clr
  Register SC (.D(multiplexer_2_out), .Q(SC_q));  // open: en, clk, clr
  RAM STACK (.addr(SC_q), .dout({adder_1_out_2, adder_1_out}));  // open: we, oe, clk, din
  PLA #(.in_width(4), .out_width(8)) pla_1 (.in(OPCODE));  // open: out
endmodule
